// Logisim project army_hard_coding_competition.circ as structural Verilog: 7 circuits, main circuit calculator
module calculator (
  input  A3,
  input  A2,
  input  A1,
  input  A0,
  input  B3,
  input  B2,
  input  B1,
  input  B0,
  input  S1,
  input  S0,
  output Y0,
  output Y1,
  output Y2,
  output Y3,
  output Y4,
  output Y5,
  output Y6,
  output Y7
);

  wire [7:0] n4_bit_multiplier_1_y0, n4_bit_ripple_adder_1_y0, n4_bit_subtractor_1_y0;

  _4_bit_subtractor u_4_bit_subtractor_1 (
    .B0(B0), .B1(B1), .B2(B2), .B3(B3), .A0(A0), .A1(A1), .A2(A2), .A3(A3), .Y0(n4_bit_subtractor_1_y0[0]),
    .Y1(n4_bit_subtractor_1_y0[1]), .Y2(n4_bit_subtractor_1_y0[2]), .Y3(n4_bit_subtractor_1_y0[7]));
  _4_bit_multiplier u_4_bit_multiplier_1 (
    .A3(A3), .A2(A2), .A1(A1), .A0(A0), .B3(B3), .B2(B2), .B1(B1), .B0(B0), .Y7(n4_bit_multiplier_1_y0[7]),
    .Y6(n4_bit_multiplier_1_y0[6]), .Y5(n4_bit_multiplier_1_y0[5]), .Y4(n4_bit_multiplier_1_y0[4]),
    .Y3(n4_bit_multiplier_1_y0[3]), .Y2(n4_bit_multiplier_1_y0[2]), .Y1(n4_bit_multiplier_1_y0[1]),
    .Y0(n4_bit_multiplier_1_y0[0]));
  _4_Bit_Ripple_adder u_4_bit_ripple_adder_1 (
    .A0(A0), .B0(B0), .A1(A1), .B1(B1), .A2(A2), .B2(B2), .A3(A3), .B3(B3), .Y0(n4_bit_ripple_adder_1_y0[0]),
    .Y1(n4_bit_ripple_adder_1_y0[1]), .Y2(n4_bit_ripple_adder_1_y0[2]), .Y3(n4_bit_ripple_adder_1_y0[7]));  // open: Cout
  Multiplexer #(.select(2), .width(8)) multiplexer_1 (
    .in0({{5{n4_bit_ripple_adder_1_y0[7]}}, n4_bit_ripple_adder_1_y0[2:0]}),
    .in1({{5{n4_bit_subtractor_1_y0[7]}}, n4_bit_subtractor_1_y0[2:0]}), .in2(n4_bit_multiplier_1_y0),
    .out({Y7, Y6, Y5, Y4, Y3, Y2, Y1, Y0}), .sel({S1, S0}));  // open: in3, en
endmodule

module _4_Bit_Ripple_adder (
  input  A0,
  input  A1,
  input  A2,
  input  A3,
  input  B1,
  input  B2,
  input  B3,
  input  B0,
  output Cout,
  output Y0,
  output Y1,
  output Y2,
  output Y3
);

  wire full_adder_1_cout, full_adder_2_cout, full_adder_3_cout;

  full_adder full_adder_1 (.Cin(1'b0), .Y(A0), .Z(B0), .SUM(Y0), .Cout(full_adder_1_cout));
  full_adder full_adder_2 (.Cin(full_adder_1_cout), .Y(A1), .Z(B1), .SUM(Y1), .Cout(full_adder_2_cout));
  full_adder full_adder_3 (.Cin(full_adder_2_cout), .Y(A2), .Z(B2), .SUM(Y2), .Cout(full_adder_3_cout));
  full_adder full_adder_4 (.Cin(full_adder_3_cout), .Y(A3), .Z(B3), .SUM(Y3), .Cout(Cout));
endmodule

module bin_multiplie_4bit_input (
  input  A,
  input  B,
  input  C,
  input  D,
  input  E,
  input  F,
  input  G,
  input  H,
  output u,
  output v,
  output w,
  output x,
  output q,
  output r,
  output s,
  output t,
  output m,
  output n,
  output o,
  output p,
  output i,
  output j,
  output k,
  output l
);

  and and_1 (u, E, A);
  and and_2 (v, E, B);
  and and_3 (w, E, C);
  and and_4 (x, E, D);
  and and_5 (q, F, A);
  and and_6 (r, F, B);
  and and_7 (s, F, C);
  and and_8 (t, F, D);
  and and_9 (m, G, A);
  and and_10 (n, G, B);
  and and_11 (o, G, C);
  and and_12 (p, G, D);
  and and_13 (i, H, A);
  and and_14 (j, H, B);
  and and_15 (k, H, C);
  and and_16 (l, H, D);
endmodule

module _4_bit_multiplier (
  input  A3,
  input  A2,
  input  A1,
  input  A0,
  input  B3,
  input  B2,
  input  B1,
  input  B0,
  output Y7,
  output Y6,
  output Y5,
  output Y4,
  output Y3,
  output Y2,
  output Y1,
  output Y0
);

  wire and_1_out, and_2_out, and_3_out, and_4_out, bin_multiplie_4bit_input_1_i,
       bin_multiplie_4bit_input_1_j, bin_multiplie_4bit_input_1_k, bin_multiplie_4bit_input_1_l,
       bin_multiplie_4bit_input_1_m, bin_multiplie_4bit_input_1_n, bin_multiplie_4bit_input_1_o,
       bin_multiplie_4bit_input_1_p, bin_multiplie_4bit_input_1_q, bin_multiplie_4bit_input_1_r,
       bin_multiplie_4bit_input_1_s, bin_multiplie_4bit_input_1_t, bin_multiplie_4bit_input_1_u,
       bin_multiplie_4bit_input_1_v, bin_multiplie_4bit_input_1_w, bin_multiplie_4bit_input_1_x,
       n8_bit_ripple_adder_1_y0, n8_bit_ripple_adder_1_y1, n8_bit_ripple_adder_1_y2,
       n8_bit_ripple_adder_1_y3, n8_bit_ripple_adder_1_y4, n8_bit_ripple_adder_1_y5,
       n8_bit_ripple_adder_1_y6, n8_bit_ripple_adder_1_y7, n8_bit_ripple_adder_2_y0,
       n8_bit_ripple_adder_2_y1, n8_bit_ripple_adder_2_y2, n8_bit_ripple_adder_2_y3,
       n8_bit_ripple_adder_2_y4, n8_bit_ripple_adder_2_y5, n8_bit_ripple_adder_2_y6,
       n8_bit_ripple_adder_2_y7, n8_bit_ripple_adder_3_y0, n8_bit_ripple_adder_3_y1,
       n8_bit_ripple_adder_3_y2, n8_bit_ripple_adder_3_y3, n8_bit_ripple_adder_3_y4,
       n8_bit_ripple_adder_3_y5, n8_bit_ripple_adder_3_y6, n8_bit_ripple_adder_3_y7,
       n8_bit_ripple_adder_4_y0, n8_bit_ripple_adder_4_y1, n8_bit_ripple_adder_4_y2,
       n8_bit_ripple_adder_4_y3, n8_bit_ripple_adder_4_y4, n8_bit_ripple_adder_4_y5,
       n8_bit_ripple_adder_4_y6, n8_bit_ripple_adder_4_y7, n8_bit_ripple_adder_5_y0,
       n8_bit_ripple_adder_5_y1, n8_bit_ripple_adder_5_y2, n8_bit_ripple_adder_5_y3,
       n8_bit_ripple_adder_5_y4, n8_bit_ripple_adder_5_y5, n8_bit_ripple_adder_5_y6,
       n8_bit_ripple_adder_5_y7, n8_bit_ripple_adder_6_y0, n8_bit_ripple_adder_6_y1,
       n8_bit_ripple_adder_6_y2, n8_bit_ripple_adder_6_y3, n8_bit_ripple_adder_6_y4,
       n8_bit_ripple_adder_6_y5, n8_bit_ripple_adder_6_y6, n8_bit_ripple_adder_6_y7;

  bin_multiplie_4bit_input bin_multiplie_4bit_input_1 (
    .A(A3), .B(A2), .C(A1), .D(A0), .E(B3), .F(B2), .G(B1), .H(B0), .u(bin_multiplie_4bit_input_1_u),
    .v(bin_multiplie_4bit_input_1_v), .w(bin_multiplie_4bit_input_1_w), .x(bin_multiplie_4bit_input_1_x),
    .q(bin_multiplie_4bit_input_1_q), .r(bin_multiplie_4bit_input_1_r), .s(bin_multiplie_4bit_input_1_s),
    .t(bin_multiplie_4bit_input_1_t), .m(bin_multiplie_4bit_input_1_m), .n(bin_multiplie_4bit_input_1_n),
    .o(bin_multiplie_4bit_input_1_o), .p(bin_multiplie_4bit_input_1_p), .i(bin_multiplie_4bit_input_1_i),
    .j(bin_multiplie_4bit_input_1_j), .k(bin_multiplie_4bit_input_1_k), .l(bin_multiplie_4bit_input_1_l));
  and and_1 (and_1_out, A3, B3);
  and and_2 (and_2_out, A2, B3);
  and and_3 (and_3_out, A1, B3);
  and and_4 (and_4_out, A0, B3);
  _8_bit_ripple_adder u_8_bit_ripple_adder_1 (
    .A0(bin_multiplie_4bit_input_1_l), .B0(1'b0), .A1(bin_multiplie_4bit_input_1_k),
    .B1(bin_multiplie_4bit_input_1_p), .A2(bin_multiplie_4bit_input_1_j), .B2(bin_multiplie_4bit_input_1_o),
    .A3(bin_multiplie_4bit_input_1_i), .B3(bin_multiplie_4bit_input_1_n), .A4(bin_multiplie_4bit_input_1_m),
    .B4(bin_multiplie_4bit_input_1_i), .A5(bin_multiplie_4bit_input_1_m), .B5(bin_multiplie_4bit_input_1_i),
    .A6(bin_multiplie_4bit_input_1_m), .B6(bin_multiplie_4bit_input_1_i), .A7(bin_multiplie_4bit_input_1_m),
    .B7(bin_multiplie_4bit_input_1_i), .Y0(n8_bit_ripple_adder_1_y0), .Y1(n8_bit_ripple_adder_1_y1),
    .Y2(n8_bit_ripple_adder_1_y2), .Y3(n8_bit_ripple_adder_1_y3), .Y4(n8_bit_ripple_adder_1_y4),
    .Y5(n8_bit_ripple_adder_1_y5), .Y6(n8_bit_ripple_adder_1_y6), .Y7(n8_bit_ripple_adder_1_y7));  // open: Cout
  _8_bit_ripple_adder u_8_bit_ripple_adder_2 (
    .A0(n8_bit_ripple_adder_1_y0), .B0(1'b0), .A1(n8_bit_ripple_adder_1_y1), .B1(1'b0),
    .A2(n8_bit_ripple_adder_1_y2), .B2(bin_multiplie_4bit_input_1_t), .A3(n8_bit_ripple_adder_1_y3),
    .B3(bin_multiplie_4bit_input_1_s), .A4(n8_bit_ripple_adder_1_y4), .B4(bin_multiplie_4bit_input_1_r),
    .A5(n8_bit_ripple_adder_1_y5), .B5(bin_multiplie_4bit_input_1_q), .A6(n8_bit_ripple_adder_1_y6),
    .B6(bin_multiplie_4bit_input_1_q), .A7(n8_bit_ripple_adder_1_y7), .B7(bin_multiplie_4bit_input_1_q),
    .Y0(n8_bit_ripple_adder_2_y0), .Y1(n8_bit_ripple_adder_2_y1), .Y2(n8_bit_ripple_adder_2_y2),
    .Y3(n8_bit_ripple_adder_2_y3), .Y4(n8_bit_ripple_adder_2_y4), .Y5(n8_bit_ripple_adder_2_y5),
    .Y6(n8_bit_ripple_adder_2_y6), .Y7(n8_bit_ripple_adder_2_y7));  // open: Cout
  _8_bit_ripple_adder u_8_bit_ripple_adder_3 (
    .A0(n8_bit_ripple_adder_2_y0), .B0(1'b0), .A1(n8_bit_ripple_adder_2_y1), .B1(1'b0),
    .A2(n8_bit_ripple_adder_2_y2), .B2(1'b0), .A3(n8_bit_ripple_adder_2_y3),
    .B3(bin_multiplie_4bit_input_1_x), .A4(n8_bit_ripple_adder_2_y4), .B4(bin_multiplie_4bit_input_1_w),
    .A5(n8_bit_ripple_adder_2_y5), .B5(bin_multiplie_4bit_input_1_v), .A6(n8_bit_ripple_adder_2_y6),
    .B6(bin_multiplie_4bit_input_1_u), .A7(n8_bit_ripple_adder_2_y7), .B7(bin_multiplie_4bit_input_1_u),
    .Y0(n8_bit_ripple_adder_3_y0), .Y1(n8_bit_ripple_adder_3_y1), .Y2(n8_bit_ripple_adder_3_y2),
    .Y3(n8_bit_ripple_adder_3_y3), .Y4(n8_bit_ripple_adder_3_y4), .Y5(n8_bit_ripple_adder_3_y5),
    .Y6(n8_bit_ripple_adder_3_y6), .Y7(n8_bit_ripple_adder_3_y7));  // open: Cout
  _8_bit_ripple_adder u_8_bit_ripple_adder_4 (
    .A0(n8_bit_ripple_adder_3_y0), .B0(1'b0), .A1(n8_bit_ripple_adder_3_y1), .B1(1'b0),
    .A2(n8_bit_ripple_adder_3_y2), .B2(1'b0), .A3(n8_bit_ripple_adder_3_y3), .B3(1'b0),
    .A4(n8_bit_ripple_adder_3_y4), .B4(and_4_out), .A5(n8_bit_ripple_adder_3_y5), .B5(and_3_out),
    .A6(n8_bit_ripple_adder_3_y6), .B6(and_2_out), .A7(n8_bit_ripple_adder_3_y7), .B7(and_1_out),
    .Y0(n8_bit_ripple_adder_4_y0), .Y1(n8_bit_ripple_adder_4_y1), .Y2(n8_bit_ripple_adder_4_y2),
    .Y3(n8_bit_ripple_adder_4_y3), .Y4(n8_bit_ripple_adder_4_y4), .Y5(n8_bit_ripple_adder_4_y5),
    .Y6(n8_bit_ripple_adder_4_y6), .Y7(n8_bit_ripple_adder_4_y7));  // open: Cout
  _8_bit_ripple_adder u_8_bit_ripple_adder_5 (
    .A0(n8_bit_ripple_adder_4_y0), .B0(1'b0), .A1(n8_bit_ripple_adder_4_y1), .B1(1'b0),
    .A2(n8_bit_ripple_adder_4_y2), .B2(1'b0), .A3(n8_bit_ripple_adder_4_y3), .B3(1'b0),
    .A4(n8_bit_ripple_adder_4_y4), .B4(1'b0), .A5(n8_bit_ripple_adder_4_y5), .B5(and_4_out),
    .A6(n8_bit_ripple_adder_4_y6), .B6(and_3_out), .A7(n8_bit_ripple_adder_4_y7), .B7(and_2_out),
    .Y0(n8_bit_ripple_adder_5_y0), .Y1(n8_bit_ripple_adder_5_y1), .Y2(n8_bit_ripple_adder_5_y2),
    .Y3(n8_bit_ripple_adder_5_y3), .Y4(n8_bit_ripple_adder_5_y4), .Y5(n8_bit_ripple_adder_5_y5),
    .Y6(n8_bit_ripple_adder_5_y6), .Y7(n8_bit_ripple_adder_5_y7));  // open: Cout
  _8_bit_ripple_adder u_8_bit_ripple_adder_6 (
    .A0(n8_bit_ripple_adder_5_y0), .B0(1'b0), .A1(n8_bit_ripple_adder_5_y1), .B1(1'b0),
    .A2(n8_bit_ripple_adder_5_y2), .B2(1'b0), .A3(n8_bit_ripple_adder_5_y3), .B3(1'b0),
    .A4(n8_bit_ripple_adder_5_y4), .B4(1'b0), .A5(n8_bit_ripple_adder_5_y5), .B5(1'b0),
    .A6(n8_bit_ripple_adder_5_y6), .B6(and_4_out), .A7(n8_bit_ripple_adder_5_y7), .B7(and_3_out),
    .Y0(n8_bit_ripple_adder_6_y0), .Y1(n8_bit_ripple_adder_6_y1), .Y2(n8_bit_ripple_adder_6_y2),
    .Y3(n8_bit_ripple_adder_6_y3), .Y4(n8_bit_ripple_adder_6_y4), .Y5(n8_bit_ripple_adder_6_y5),
    .Y6(n8_bit_ripple_adder_6_y6), .Y7(n8_bit_ripple_adder_6_y7));  // open: Cout
  _8_bit_ripple_adder u_8_bit_ripple_adder_7 (
    .A0(n8_bit_ripple_adder_6_y0), .B0(1'b0), .A1(n8_bit_ripple_adder_6_y1), .B1(1'b0),
    .A2(n8_bit_ripple_adder_6_y2), .B2(1'b0), .A3(n8_bit_ripple_adder_6_y3), .B3(1'b0),
    .A4(n8_bit_ripple_adder_6_y4), .B4(1'b0), .A5(n8_bit_ripple_adder_6_y5), .B5(1'b0),
    .A6(n8_bit_ripple_adder_6_y6), .B6(1'b0), .A7(n8_bit_ripple_adder_6_y7), .B7(and_4_out), .Y0(Y0),
    .Y1(Y1), .Y2(Y2), .Y3(Y3), .Y4(Y4), .Y5(Y5), .Y6(Y6), .Y7(Y7));  // open: Cout
endmodule

module full_adder (
  input  Cin,
  input  Y,
  input  Z,
  output SUM,
  output Cout
);

  wire and_1_out, and_2_out, and_3_out, xor_1_out;

  and and_1 (and_1_out, Z, Cin);
  and and_2 (and_2_out, Cin, Y);
  and and_3 (and_3_out, Y, Z);
  xor xor_1 (xor_1_out, Z, Y);
  xor xor_2 (SUM, xor_1_out, Cin);
  or or_1 (Cout, and_1_out, and_2_out, and_3_out);
endmodule

module _8_bit_ripple_adder (
  input  A0,
  input  A1,
  input  A2,
  input  A3,
  input  A4,
  input  A5,
  input  A6,
  input  A7,
  input  B0,
  input  B1,
  input  B2,
  input  B3,
  input  B4,
  input  B5,
  input  B6,
  input  B7,
  output Cout,
  output Y0,
  output Y1,
  output Y2,
  output Y3,
  output Y4,
  output Y5,
  output Y6,
  output Y7
);

  wire full_adder_1_cout, full_adder_2_cout, full_adder_3_cout, full_adder_4_cout, full_adder_5_cout,
       full_adder_6_cout, full_adder_7_cout;

  full_adder full_adder_1 (.Cin(1'b0), .Y(A0), .Z(B0), .SUM(Y0), .Cout(full_adder_1_cout));
  full_adder full_adder_2 (.Cin(full_adder_1_cout), .Y(A1), .Z(B1), .SUM(Y1), .Cout(full_adder_2_cout));
  full_adder full_adder_3 (.Cin(full_adder_2_cout), .Y(A2), .Z(B2), .SUM(Y2), .Cout(full_adder_3_cout));
  full_adder full_adder_4 (.Cin(full_adder_3_cout), .Y(A3), .Z(B3), .SUM(Y3), .Cout(full_adder_4_cout));
  full_adder full_adder_5 (.Cin(full_adder_4_cout), .Y(A4), .Z(B4), .SUM(Y4), .Cout(full_adder_5_cout));
  full_adder full_adder_6 (.Cin(full_adder_5_cout), .Y(A5), .Z(B5), .SUM(Y5), .Cout(full_adder_6_cout));
  full_adder full_adder_7 (.Cin(full_adder_6_cout), .Y(A6), .Z(B6), .SUM(Y6), .Cout(full_adder_7_cout));
  full_adder full_adder_8 (.Cin(full_adder_7_cout), .Y(A7), .Z(B7), .SUM(Y7), .Cout(Cout));
endmodule

module _4_bit_subtractor (
  input  B0,
  input  B1,
  input  B2,
  input  B3,
  input  A0,
  input  A1,
  input  A2,
  input  A3,
  output Y0,
  output Y1,
  output Y2,
  output Y3
);

  wire n4_bit_ripple_adder_1_y0, n4_bit_ripple_adder_1_y1, n4_bit_ripple_adder_1_y2,
       n4_bit_ripple_adder_1_y3, not_1_out, not_2_out, not_3_out, not_4_out, not_5_out;

  not not_1 (not_1_out, 1'b0);
  _4_Bit_Ripple_adder u_4_bit_ripple_adder_1 (
    .A0(not_2_out), .B0(not_1_out), .A1(not_3_out), .B1(1'b0), .A2(not_4_out), .B2(1'b0), .A3(not_5_out),
    .B3(1'b0), .Y0(n4_bit_ripple_adder_1_y0), .Y1(n4_bit_ripple_adder_1_y1), .Y2(n4_bit_ripple_adder_1_y2),
    .Y3(n4_bit_ripple_adder_1_y3));  // open: Cout
  not not_2 (not_2_out, B0);
  not not_3 (not_3_out, B1);
  not not_4 (not_4_out, B2);
  not not_5 (not_5_out, B3);
  _4_Bit_Ripple_adder u_4_bit_ripple_adder_2 (
    .A0(n4_bit_ripple_adder_1_y0), .B0(A0), .A1(n4_bit_ripple_adder_1_y1), .B1(A1),
    .A2(n4_bit_ripple_adder_1_y2), .B2(A2), .A3(n4_bit_ripple_adder_1_y3), .B3(A3), .Y0(Y0), .Y1(Y1),
    .Y2(Y2), .Y3(Y3));  // open: Cout
endmodule
